// Logisim project My mini computer 2207027.circ as structural Verilog: 23 circuits, main circuit main
module main (
);

  wire Clock_out, control_unit_1_clock_2, control_unit_1_memory_store, Reset_out;
  wire [5:0] control_unit_1_address_bus;
  wire [24:0] control_unit_1_acc_out, control_unit_1_memory_input_value, ram_1_data;

  Button Reset (.out(Reset_out));
  // Probe on control_unit_1_acc_out
  Clock Clock (.out(Clock_out));
  Control_Unit control_unit_1 (
    .Reset(Reset_out), .clock(Clock_out), .Acc_Out(control_unit_1_acc_out), .Clock_2(control_unit_1_clock_2),
    .Memory_Out(ram_1_data), .Address_Bus(control_unit_1_address_bus),
    .Memory_Input_Value(control_unit_1_memory_input_value), .Memory_Store(control_unit_1_memory_store));
  RAM #(.addrWidth(6), .dataWidth(25), .bus("separate")) ram_1 (
    .addr(control_unit_1_address_bus), .din(control_unit_1_memory_input_value), .data(ram_1_data),
    .str(control_unit_1_memory_store), .clk(control_unit_1_clock_2));  // open: sel, ld, clr

  // Notes on the sheet:
  //   2207027
  //   AND
  //   ADD
  //   STORE
  //   BUN
  //   BSB
  //   LOAD
  //   ISZ
  //   JZ
  //   PUSH
  //   POP
  //   HALT
  //   NEG
  //   MUL
  //   JN
endmodule

// A/S
module _5_bit_parallel_adder (
  input  [4:0] A,
  input  [4:0] B,
  input  Cin,
  output Cout,
  output Overflow,
  output [4:0] Sout
);

  wire and_1_out, and_2_out, and_3_out, and_4_out, and_5_out, and_6_out, and_7_out, and_8_out, and_9_out,
       and_10_out, and_11_out, and_12_out, and_13_out, and_14_out, and_15_out, C1_out, C2_out, C3_out,
       C4_out, G0_out, G1_out, G2_out, G3_out, G4_out, P0_out, P1_out, P2_out, P3_out, P4_out;

  xor xor_1 (Overflow, Cout, C4_out);
  and G4 (G4_out, B[4], A[4]);
  and and_1 (and_1_out, G3_out, P4_out);
  or C5 (Cout, G4_out, and_1_out, and_2_out, and_3_out, and_4_out, and_5_out);
  xor P4 (P4_out, A[4], B[4]);
  and and_2 (and_2_out, P4_out, P3_out, G2_out);
  and and_3 (and_3_out, P4_out, P3_out, P2_out, G1_out);
  and and_4 (and_4_out, P4_out, P3_out, P2_out, P1_out, G0_out);
  and and_5 (and_5_out, P4_out, P3_out, P2_out, P1_out, P0_out, Cin);
  and G3 (G3_out, B[3], A[3]);
  and and_6 (and_6_out, P3_out, G2_out);
  or C4 (C4_out, G3_out, and_6_out, and_7_out, and_9_out, and_8_out);
  xor xor_2 (Sout[4], P4_out, C4_out);
  xor P3 (P3_out, A[3], B[3]);
  and and_7 (and_7_out, P3_out, P2_out, G1_out);
  and and_8 (and_8_out, P3_out, P2_out, P1_out, P0_out, Cin);
  and and_9 (and_9_out, P3_out, P2_out, P1_out, G0_out);
  and G2 (G2_out, B[2], A[2]);
  and and_10 (and_10_out, P2_out, G1_out);
  or C3 (C3_out, G2_out, and_10_out, and_11_out, and_12_out);
  xor xor_3 (Sout[3], P3_out, C3_out);
  xor P2 (P2_out, A[2], B[2]);
  and and_11 (and_11_out, P2_out, P1_out, G0_out);
  and and_12 (and_12_out, P2_out, P1_out, P0_out, Cin);
  and G1 (G1_out, B[1], A[1]);
  and and_13 (and_13_out, P1_out, G0_out);
  or C2 (C2_out, G1_out, and_13_out, and_14_out);
  xor xor_4 (Sout[2], P2_out, C2_out);
  xor P1 (P1_out, A[1], B[1]);
  and and_14 (and_14_out, P1_out, P0_out, Cin);
  and G0 (G0_out, B[0], A[0]);
  xor xor_5 (Sout[1], P1_out, C1_out);
  xor P0 (P0_out, A[0], B[0]);
  and and_15 (and_15_out, Cin, P0_out);
  or C1 (C1_out, G0_out, and_15_out);
  xor xor_6 (Sout[0], P0_out, Cin);
endmodule

// Adder
module _25_bit_adder_subtractor (
  input  [24:0] A,
  input  [24:0] B,
  input  Control,
  output Cout,
  output Overflow,
  output [24:0] Result
);

  wire n5_bit_parallel_adder_1_cout, n5_bit_parallel_adder_3_cout, n5_bit_parallel_adder_4_cout,
       n5_bit_parallel_adder_5_cout;
  wire [4:0] xor_1_out, xor_1_out_3, xor_1_out_4, xor_1_out_5;
  wire [9:5] xor_1_out_2;

  _5_bit_parallel_adder u_5_bit_parallel_adder_1 (
    .Cout(n5_bit_parallel_adder_1_cout), .A(A[19:15]), .B(xor_1_out_4), .Sout(Result[19:15]),
    .Cin(n5_bit_parallel_adder_4_cout));  // open: Overflow
  _5_bit_parallel_adder u_5_bit_parallel_adder_2 (
    .Cout(Cout), .Overflow(Overflow), .A(A[24:20]), .B(xor_1_out_5), .Sout(Result[24:20]),
    .Cin(n5_bit_parallel_adder_1_cout));
  _5_bit_parallel_adder u_5_bit_parallel_adder_3 (
    .Cout(n5_bit_parallel_adder_3_cout), .A(A[9:5]), .B(xor_1_out_2), .Sout(Result[9:5]),
    .Cin(n5_bit_parallel_adder_5_cout));  // open: Overflow
  _5_bit_parallel_adder u_5_bit_parallel_adder_4 (
    .Cout(n5_bit_parallel_adder_4_cout), .A(A[14:10]), .B(xor_1_out_3), .Sout(Result[14:10]),
    .Cin(n5_bit_parallel_adder_3_cout));  // open: Overflow
  assign {xor_1_out_5, xor_1_out_4, xor_1_out_3, xor_1_out_2, xor_1_out} = B ^ {25{Control}};  // XOR_Gate xor_1, 25 bits wide
  _5_bit_parallel_adder u_5_bit_parallel_adder_5 (
    .Cout(n5_bit_parallel_adder_5_cout), .A(A[4:0]), .B(xor_1_out), .Sout(Result[4:0]), .Cin(Control));  // open: Overflow
endmodule

module ALU (
  input  [1:0] Control_or_and_add_sub,
  input  [24:0] A,
  input  [24:0] B,
  output [24:0] Result,
  output [3:0] flags_NZOC
);

  wire n25_bit_adder_subtractor_1_cout, n25_bit_adder_subtractor_1_overflow;
  wire [24:0] and_1_out, n25_bit_adder_subtractor_1_result, or_1_out;

  and Cout (flags_NZOC[0], Control_or_and_add_sub[1], n25_bit_adder_subtractor_1_cout);
  _25_bit_adder_subtractor u_25_bit_adder_subtractor_1 (
    .Cout(n25_bit_adder_subtractor_1_cout), .Overflow(n25_bit_adder_subtractor_1_overflow), .A(A), .B(B),
    .Result(n25_bit_adder_subtractor_1_result), .Control(Control_or_and_add_sub[0]));
  and overflow (flags_NZOC[1], Control_or_and_add_sub[1], n25_bit_adder_subtractor_1_overflow);
  assign and_1_out = A & B;  // AND_Gate and_1, 25 bits wide
  assign or_1_out = A | B;  // OR_Gate or_1, 25 bits wide
  _4x1_Mux u_4x1_mux_1 (
    .in_3(and_1_out), .in_4(or_1_out), .in_5(n25_bit_adder_subtractor_1_result),
    .in_6(n25_bit_adder_subtractor_1_result), .in_1(Control_or_and_add_sub[1]),
    .in_2(Control_or_and_add_sub[0]), .out_7(Result));
  Zero_Flag Zero (.in_1(Result), .out_2(flags_NZOC[2]));
  Sign_Flag sign (.in_1(Result), .out_2(flags_NZOC[3]));

  // Other names for the same wires on the sheet: Cin = Control_or_and_add_sub[0]; AddSub = Control_or_and_add_sub[1]

  // Notes on the sheet:
  //   2207027
endmodule

module _4x1_Mux (
  input  in_1,
  input  in_2,
  input  [24:0] in_3,
  input  [24:0] in_4,
  input  [24:0] in_5,
  input  [24:0] in_6,
  output [24:0] out_7
);

  wire [24:0] and_1_out, and_2_out, and_3_out, and_4_out, not_1_out, not_2_out;

  assign not_1_out = ~{25{in_2}};  // NOT_Gate not_1, 25 bits wide
  assign not_2_out = ~{25{in_1}};  // NOT_Gate not_2, 25 bits wide
  assign and_1_out = in_3 & not_1_out & not_2_out;  // AND_Gate and_1, 25 bits wide
  assign and_2_out = in_4 & {25{in_2}} & not_2_out;  // AND_Gate and_2, 25 bits wide
  assign and_3_out = in_5 & not_1_out & {25{in_1}};  // AND_Gate and_3, 25 bits wide
  assign and_4_out = in_6 & {25{in_2}} & {25{in_1}};  // AND_Gate and_4, 25 bits wide
  assign out_7 = and_1_out | and_2_out | and_3_out | and_4_out;  // OR_Gate or_1, 25 bits wide
endmodule

module Sign_Flag (
  input  [24:0] in_1,
  output out_2
);


  assign out_2 = in_1[24];
endmodule

module Zero_Flag (
  input  [24:0] in_1,
  output out_2
);

  wire or_1_out;

  or or_1 (or_1_out, in_1[0], in_1[1], in_1[2], in_1[3], in_1[4], in_1[5], in_1[6], in_1[7], in_1[8], in_1[9], in_1[10], in_1[11], in_1[12], in_1[13], in_1[14], in_1[15], in_1[16], in_1[17], in_1[18], in_1[19], in_1[20], in_1[21], in_1[22], in_1[23], in_1[24]);
  not not_1 (out_2, or_1_out);
endmodule

module sequence_decoder (
  input  Reset,
  input  Clk,
  input  Q0,
  input  Q_1,
  input  [4:0] Count,
  output Cl__A__Q_1,
  output LOad__M__Q__Cnt,
  output Load_A,
  output C0,
  output C1,
  output Shr,
  output Dec_Cnt,
  output Running
);

  wire nor_1_out, or_1_out, sequence_decoder_helper_1_da, sequence_decoder_helper_1_db,
       sequence_decoder_helper_1_dc, T0, T2, T4, T6, T7;
  wire [2:0] T;

  nor nor_1 (nor_1_out, Count[0], Count[1], Count[2], Count[3], Count[4]);
  Decoder #(.select(3), .enable("false")) decoder_1 (
    .out0(T0), .out1(Cl__A__Q_1), .out2(T2), .out3(C0), .out4(T4), .out5(Dec_Cnt), .out6(T6), .out7(T7),
    .sel(T));
  sequence_decoder_helper sequence_decoder_helper_1 (
    .Q({Q0, Q_1}), .T(T), .C(nor_1_out), .DA(sequence_decoder_helper_1_da),
    .DB(sequence_decoder_helper_1_db), .DC(sequence_decoder_helper_1_dc));
  D_Flip_Flop d_ff_1 (.clk(Clk), .D(sequence_decoder_helper_1_da), .Q(T[0]), .reset(Reset));  // open: Qn, preset, en
  D_Flip_Flop d_ff_2 (.clk(Clk), .D(sequence_decoder_helper_1_db), .Q(T[1]), .reset(Reset));  // open: Qn, preset, en
  D_Flip_Flop d_ff_3 (.clk(Clk), .D(sequence_decoder_helper_1_dc), .Q(T[2]), .reset(Reset));  // open: Qn, preset, en
  or or_1 (or_1_out, T7, T0);
  not not_1 (Running, or_1_out);
  or or_2 (Load_A, C0, T4);
  or or_3 (C1, C0, T4);

  assign LOad__M__Q__Cnt = Cl__A__Q_1;
  assign Shr = Dec_Cnt;

  // Other names for the same wires on the sheet: T1 = Cl__A__Q_1; T3 = C0; T5 = Dec_Cnt
endmodule

module sequence_decoder_helper (
  input  [1:0] Q,
  input  [2:0] T,
  input  C,
  output DA,
  output DB,
  output DC
);

  wire and_1_out, and_2_out, and_3_out, and_4_out, and_5_out, or_4_out, or_5_out, Q0, Q1, Q2, Q3, T0, T1, T2,
       T3, T4, T5, T6, T7;

  or or_1 (DB, T1, and_2_out, T5, T6, T6, T7);
  or or_2 (DC, T5, and_3_out, T3, T4, and_4_out, T7);
  Decoder #(.select(2), .enable("false")) decoder_1 (.out0(Q0), .out1(Q1), .out2(Q2), .out3(Q3), .sel(Q));
  Decoder #(.select(3), .enable("false")) decoder_2 (
    .out0(T0), .out1(T1), .out2(T2), .out3(T3), .out4(T4), .out5(T5), .out6(T6), .out7(T7), .sel(T));
  or or_3 (DA, T0, and_1_out, T3, T4, and_5_out, T7);
  and and_1 (and_1_out, T2, or_4_out);
  and and_2 (and_2_out, T2, Q2);
  and and_3 (and_3_out, T2, or_5_out);
  and and_4 (and_4_out, T6, C);
  or or_4 (or_4_out, Q0, Q2, Q3);
  and and_5 (and_5_out, T6, C);
  or or_5 (or_5_out, Q0, Q1, Q3);
endmodule

// MUL
module _25_bit_multiplier (
  input  [24:0] M_input,
  input  [24:0] Q_input,
  input  Reset,
  input  clock,
  output Running,
  output [24:0] out_6,
  output [24:0] out_7
);

  wire A_out, or_1_out, Q__1_q0, Q_out, sequence_decoder_1_cl__a__q_1, sequence_decoder_1_dec_cnt,
       sequence_decoder_1_load__m__q__cnt, sequence_decoder_1_load_a, sequence_decoder_1_shr;
  wire [1:0] sequence_decoder_1_c0;
  wire [4:0] counter_1_q;
  wire [24:0] alu_1_result, M_q24;

  sequence_decoder sequence_decoder_1 (
    .Reset(Reset), .Clk(clock), .Q0(out_7[0]), .Q_1(Q__1_q0), .Count(counter_1_q), .Running(Running),
    .Cl__A__Q_1(sequence_decoder_1_cl__a__q_1), .LOad__M__Q__Cnt(sequence_decoder_1_load__m__q__cnt),
    .Load_A(sequence_decoder_1_load_a), .C0(sequence_decoder_1_c0[0]), .C1(sequence_decoder_1_c0[1]),
    .Shr(sequence_decoder_1_shr), .Dec_Cnt(sequence_decoder_1_dec_cnt));
  or or_1 (or_1_out, sequence_decoder_1_load__m__q__cnt, sequence_decoder_1_dec_cnt);
  Counter #(.width(5), .max('h1f)) counter_1 (
    .load(or_1_out), .D(5'b11001), .count(sequence_decoder_1_dec_cnt), .Q(counter_1_q), .clk(clock));  // open: carry, clr
  Shift_Register #(.length(25)) M (
    .shift(1'b0), .clk(clock), .load(sequence_decoder_1_load__m__q__cnt), .d0(M_input[24]), .q0(M_q24[24]),
    .d1(M_input[23]), .q1(M_q24[23]), .d2(M_input[22]), .q2(M_q24[22]), .d3(M_input[21]), .q3(M_q24[21]),
    .d4(M_input[20]), .q4(M_q24[20]), .d5(M_input[19]), .q5(M_q24[19]), .d6(M_input[18]), .q6(M_q24[18]),
    .d7(M_input[17]), .q7(M_q24[17]), .d8(M_input[16]), .q8(M_q24[16]), .d9(M_input[15]), .q9(M_q24[15]),
    .d10(M_input[14]), .q10(M_q24[14]), .d11(M_input[13]), .q11(M_q24[13]), .d12(M_input[12]),
    .q12(M_q24[12]), .d13(M_input[11]), .q13(M_q24[11]), .d14(M_input[10]), .q14(M_q24[10]),
    .d15(M_input[9]), .q15(M_q24[9]), .d16(M_input[8]), .q16(M_q24[8]), .d17(M_input[7]), .q17(M_q24[7]),
    .d18(M_input[6]), .q18(M_q24[6]), .d19(M_input[5]), .q19(M_q24[5]), .d20(M_input[4]), .q20(M_q24[4]),
    .d21(M_input[3]), .q21(M_q24[3]), .d22(M_input[2]), .q22(M_q24[2]), .d23(M_input[1]), .q23(M_q24[1]),
    .d24(M_input[0]), .q24(M_q24[0]));  // open: in, out, clr
  Shift_Register #(.length(25)) A (
    .shift(sequence_decoder_1_shr), .in(out_6[24]), .clk(clock), .out(A_out),
    .load(sequence_decoder_1_load_a), .clr(sequence_decoder_1_cl__a__q_1), .d0(alu_1_result[24]),
    .q0(out_6[24]), .d1(alu_1_result[23]), .q1(out_6[23]), .d2(alu_1_result[22]), .q2(out_6[22]),
    .d3(alu_1_result[21]), .q3(out_6[21]), .d4(alu_1_result[20]), .q4(out_6[20]), .d5(alu_1_result[19]),
    .q5(out_6[19]), .d6(alu_1_result[18]), .q6(out_6[18]), .d7(alu_1_result[17]), .q7(out_6[17]),
    .d8(alu_1_result[16]), .q8(out_6[16]), .d9(alu_1_result[15]), .q9(out_6[15]), .d10(alu_1_result[14]),
    .q10(out_6[14]), .d11(alu_1_result[13]), .q11(out_6[13]), .d12(alu_1_result[12]), .q12(out_6[12]),
    .d13(alu_1_result[11]), .q13(out_6[11]), .d14(alu_1_result[10]), .q14(out_6[10]), .d15(alu_1_result[9]),
    .q15(out_6[9]), .d16(alu_1_result[8]), .q16(out_6[8]), .d17(alu_1_result[7]), .q17(out_6[7]),
    .d18(alu_1_result[6]), .q18(out_6[6]), .d19(alu_1_result[5]), .q19(out_6[5]), .d20(alu_1_result[4]),
    .q20(out_6[4]), .d21(alu_1_result[3]), .q21(out_6[3]), .d22(alu_1_result[2]), .q22(out_6[2]),
    .d23(alu_1_result[1]), .q23(out_6[1]), .d24(alu_1_result[0]), .q24(out_6[0]));
  ALU alu_1 (
    .A(out_6), .B(M_q24), .Control_or_and_add_sub(sequence_decoder_1_c0), .Result(alu_1_result));  // open: flags_NZOC
  Shift_Register #(.length(25)) Q (
    .shift(sequence_decoder_1_shr), .in(A_out), .clk(clock), .out(Q_out),
    .load(sequence_decoder_1_load__m__q__cnt), .d0(Q_input[24]), .q0(out_7[24]), .d1(Q_input[23]),
    .q1(out_7[23]), .d2(Q_input[22]), .q2(out_7[22]), .d3(Q_input[21]), .q3(out_7[21]), .d4(Q_input[20]),
    .q4(out_7[20]), .d5(Q_input[19]), .q5(out_7[19]), .d6(Q_input[18]), .q6(out_7[18]), .d7(Q_input[17]),
    .q7(out_7[17]), .d8(Q_input[16]), .q8(out_7[16]), .d9(Q_input[15]), .q9(out_7[15]), .d10(Q_input[14]),
    .q10(out_7[14]), .d11(Q_input[13]), .q11(out_7[13]), .d12(Q_input[12]), .q12(out_7[12]),
    .d13(Q_input[11]), .q13(out_7[11]), .d14(Q_input[10]), .q14(out_7[10]), .d15(Q_input[9]), .q15(out_7[9]),
    .d16(Q_input[8]), .q16(out_7[8]), .d17(Q_input[7]), .q17(out_7[7]), .d18(Q_input[6]), .q18(out_7[6]),
    .d19(Q_input[5]), .q19(out_7[5]), .d20(Q_input[4]), .q20(out_7[4]), .d21(Q_input[3]), .q21(out_7[3]),
    .d22(Q_input[2]), .q22(out_7[2]), .d23(Q_input[1]), .q23(out_7[1]), .d24(Q_input[0]), .q24(out_7[0]));  // open: clr
  Shift_Register #(.length(1)) Q__1 (
    .shift(sequence_decoder_1_shr), .in(Q_out), .clk(clock), .clr(sequence_decoder_1_cl__a__q_1), .q0(Q__1_q0));  // open: out, load, d0

  // Other names for the same wires on the sheet: accumulator[24:0] = out_6
endmodule

// IR
module _4_bit_load_register (
  input  load,
  input  [3:0] Input,
  input  clock,
  input  clear,
  output [3:0] Output
);

  wire and_1_out, and_2_out, and_3_out, and_4_out, and_5_out, and_6_out, and_7_out, and_8_out, not_1_out,
       not_2_out, or_1_out, or_2_out, or_3_out, or_4_out;

  not not_1 (not_1_out, load);
  not not_2 (not_2_out, not_1_out);
  and and_1 (and_1_out, Output[0], not_1_out);
  and and_2 (and_2_out, Input[0], not_2_out);
  and and_3 (and_3_out, Output[1], not_1_out);
  and and_4 (and_4_out, Input[1], not_2_out);
  and and_5 (and_5_out, Output[2], not_1_out);
  and and_6 (and_6_out, Input[2], not_2_out);
  and and_7 (and_7_out, Output[3], not_1_out);
  and and_8 (and_8_out, Input[3], not_2_out);
  or or_1 (or_1_out, and_1_out, and_2_out);
  or or_2 (or_2_out, and_3_out, and_4_out);
  or or_3 (or_3_out, and_5_out, and_6_out);
  or or_4 (or_4_out, and_7_out, and_8_out);
  D_Flip_Flop d_ff_1 (.clk(clock), .D(or_1_out), .Q(Output[0]), .reset(clear));  // open: Qn, preset, en
  D_Flip_Flop d_ff_2 (.clk(clock), .D(or_2_out), .Q(Output[1]), .reset(clear));  // open: Qn, preset, en
  D_Flip_Flop d_ff_3 (.clk(clock), .D(or_3_out), .Q(Output[2]));  // open: Qn, preset, en, reset
  D_Flip_Flop d_ff_4 (.clk(clock), .D(or_4_out), .Q(Output[3]), .reset(clear));  // open: Qn, preset, en
endmodule

module _4_bit_load_with_counter_register (
  input  count,
  input  load,
  input  [3:0] Input,
  input  clock,
  input  clear,
  output [3:0] Outputs,
  output Cout
);

  wire and_1_out, and_2_out, and_3_out, and_4_out, and_5_out, and_6_out, and_7_out, and_8_out, and_9_out,
       and_10_out, and_11_out, and_12_out, not_1_out, not_2_out, not_3_out, not_4_out, not_5_out, not_6_out,
       not_7_out, or_1_out, or_2_out, or_3_out, or_4_out, or_5_out, or_6_out, or_7_out, or_8_out;

  not not_1 (not_1_out, load);
  not not_2 (not_2_out, Input[0]);
  not not_3 (not_3_out, Input[1]);
  not not_4 (not_4_out, Input[2]);
  not not_5 (not_5_out, Input[3]);
  and and_1 (and_1_out, count, not_1_out);
  not not_6 (not_6_out, not_1_out);
  not not_7 (not_7_out, clock);
  and and_2 (and_2_out, not_6_out, Input[0]);
  and and_3 (and_3_out, not_6_out, not_2_out);
  and and_4 (and_4_out, not_6_out, Input[1]);
  and and_5 (and_5_out, not_6_out, not_3_out);
  and and_6 (and_6_out, not_6_out, Input[2]);
  and and_7 (and_7_out, not_6_out, not_4_out);
  and and_8 (and_8_out, not_6_out, Input[3]);
  and and_9 (and_9_out, not_6_out, not_5_out);
  and and_10 (and_10_out, and_1_out, Outputs[0]);
  and and_11 (and_11_out, and_1_out, Outputs[0], Outputs[1]);
  and and_12 (and_12_out, and_1_out, Outputs[0], Outputs[1], Outputs[2]);
  or or_1 (or_1_out, and_2_out, and_1_out);
  J_K_Flip_Flop j_k_ff_1 (
    .J(or_1_out), .clk(not_7_out), .K(or_2_out), .Q(Outputs[0]), .reset(clear));  // open: Qn, preset, en
  or or_2 (or_2_out, and_1_out, and_3_out);
  or or_3 (or_3_out, and_4_out, and_10_out);
  J_K_Flip_Flop j_k_ff_2 (
    .J(or_3_out), .clk(not_7_out), .K(or_4_out), .Q(Outputs[1]), .reset(clear));  // open: Qn, preset, en
  or or_4 (or_4_out, and_10_out, and_5_out);
  or or_5 (or_5_out, and_6_out, and_11_out);
  J_K_Flip_Flop j_k_ff_3 (
    .J(or_5_out), .clk(not_7_out), .K(or_6_out), .Q(Outputs[2]), .reset(clear));  // open: Qn, preset, en
  or or_6 (or_6_out, and_11_out, and_7_out);
  or or_7 (or_7_out, and_8_out, and_12_out);
  J_K_Flip_Flop j_k_ff_4 (
    .J(or_7_out), .clk(not_7_out), .K(or_8_out), .Q(Outputs[3]), .reset(clear));  // open: Qn, preset, en
  or or_8 (or_8_out, and_12_out, and_9_out);
  and and_13 (Cout, Outputs[3], Outputs[2], Outputs[1], Outputs[0]);
endmodule

module _1_bit_load_with_counter_register (
  input  count,
  input  load,
  input  Input,
  input  clock,
  input  clear,
  output Outputs,
  output Cout
);

  wire and_1_out, and_2_out, and_3_out, not_1_out, not_2_out, not_3_out, not_4_out, or_1_out, or_2_out;

  not not_1 (not_1_out, load);
  not not_2 (not_2_out, Input);
  not not_3 (not_3_out, clock);
  and and_1 (and_1_out, count, not_1_out);
  not not_4 (not_4_out, not_1_out);
  and and_2 (and_2_out, not_4_out, Input);
  and and_3 (and_3_out, not_4_out, not_2_out);
  or or_1 (or_1_out, and_2_out, and_1_out);
  J_K_Flip_Flop j_k_ff_1 (
    .J(or_1_out), .clk(not_3_out), .K(or_2_out), .Q(Cout), .reset(clear));  // open: Qn, preset, en
  or or_2 (or_2_out, and_1_out, and_3_out);

  assign Outputs = Cout;
endmodule

module _1_bit_load_register (
  input  load,
  input  Input,
  input  clock,
  input  clear,
  output Output
);

  wire and_1_out, and_2_out, not_1_out, not_2_out, or_1_out;

  not not_1 (not_1_out, load);
  not not_2 (not_2_out, not_1_out);
  and and_1 (and_1_out, Output, not_1_out);
  and and_2 (and_2_out, Input, not_2_out);
  or or_1 (or_1_out, and_1_out, and_2_out);
  D_Flip_Flop d_ff_1 (.clk(clock), .D(or_1_out), .Q(Output), .reset(clear));  // open: Qn, preset, en
endmodule

// AC
module Accumulator (
  input  [24:0] \input ,
  input  clock,
  input  load,
  input  clear,
  output [24:0] \output 
);

  _4_bit_load_register u_4_bit_load_register_1 (
    .load(load), .Input(\input [24:21]), .clock(clock), .clear(clear), .Output(\output [24:21]));
  _4_bit_load_register u_4_bit_load_register_2 (
    .load(load), .Input(\input [20:17]), .clock(clock), .clear(clear), .Output(\output [20:17]));
  _4_bit_load_register u_4_bit_load_register_3 (
    .load(load), .Input(\input [16:13]), .clock(clock), .clear(clear), .Output(\output [16:13]));
  _4_bit_load_register u_4_bit_load_register_4 (
    .load(load), .Input(\input [12:9]), .clock(clock), .clear(clear), .Output(\output [12:9]));
  _4_bit_load_register u_4_bit_load_register_5 (
    .load(load), .Input(\input [8:5]), .clock(clock), .clear(clear), .Output(\output [8:5]));
  _4_bit_load_register u_4_bit_load_register_6 (
    .load(load), .Input(\input [4:1]), .clock(clock), .clear(clear), .Output(\output [4:1]));
  _1_bit_load_register u_1_bit_load_register_1 (
    .load(load), .Input(\input [0]), .clock(clock), .clear(clear), .Output(\output [0]));
endmodule

module MAR (
  input  [5:0] \input ,
  input  clock,
  input  load,
  input  clear,
  output [5:0] \output 
);

  _4_bit_load_register u_4_bit_load_register_1 (
    .load(load), .Input(\input [5:2]), .clock(clock), .clear(clear), .Output(\output [5:2]));
  _1_bit_load_register u_1_bit_load_register_1 (
    .load(load), .Input(\input [1]), .clock(clock), .clear(clear), .Output(\output [1]));
  _1_bit_load_register u_1_bit_load_register_2 (
    .load(load), .Input(\input [0]), .clock(clock), .clear(clear), .Output(\output [0]));
endmodule

module PC (
  input  [5:0] Input,
  input  count,
  input  load,
  input  clock,
  input  clear,
  output [5:0] Outputs
);

  wire and_1_out, and_2_out, n1_bit_load_with_counter_register_1_cout,
       n1_bit_load_with_counter_register_2_cout;

  _4_bit_load_with_counter_register u_4_bit_load_with_counter_register_1 (
    .count(and_1_out), .load(load), .Input(Input[5:2]), .clock(clock), .clear(clear), .Outputs(Outputs[5:2]));  // open: Cout
  and and_1 (and_1_out, and_2_out, n1_bit_load_with_counter_register_1_cout);
  and and_2 (and_2_out, count, n1_bit_load_with_counter_register_2_cout);
  _1_bit_load_with_counter_register u_1_bit_load_with_counter_register_1 (
    .count(and_2_out), .load(load), .Input(Input[1]), .clock(clock), .clear(clear),
    .Cout(n1_bit_load_with_counter_register_1_cout), .Outputs(Outputs[1]));
  _1_bit_load_with_counter_register u_1_bit_load_with_counter_register_2 (
    .count(count), .load(load), .Input(Input[0]), .clock(clock), .clear(clear),
    .Cout(n1_bit_load_with_counter_register_2_cout), .Outputs(Outputs[0]));
endmodule

module MBR (
  input  [24:0] Input,
  input  count,
  input  load,
  input  clock,
  input  clear,
  output [24:0] Outputs
);

  wire and_1_out, and_2_out, and_3_out, and_4_out, and_5_out, and_6_out,
       n1_bit_load_with_counter_register_1_cout, n4_bit_load_with_counter_register_2_cout,
       n4_bit_load_with_counter_register_3_cout, n4_bit_load_with_counter_register_4_cout,
       n4_bit_load_with_counter_register_5_cout, n4_bit_load_with_counter_register_6_cout;

  and and_1 (and_1_out, and_2_out, n4_bit_load_with_counter_register_2_cout);
  _4_bit_load_with_counter_register u_4_bit_load_with_counter_register_1 (
    .count(and_1_out), .load(load), .Input(Input[24:21]), .clock(clock), .clear(clear),
    .Outputs(Outputs[24:21]));  // open: Cout
  and and_2 (and_2_out, and_3_out, n4_bit_load_with_counter_register_3_cout);
  _4_bit_load_with_counter_register u_4_bit_load_with_counter_register_2 (
    .count(and_2_out), .load(load), .Input(Input[20:17]), .clock(clock), .clear(clear),
    .Cout(n4_bit_load_with_counter_register_2_cout), .Outputs(Outputs[20:17]));
  _4_bit_load_with_counter_register u_4_bit_load_with_counter_register_3 (
    .count(and_3_out), .load(load), .Input(Input[16:13]), .clock(clock), .clear(clear),
    .Cout(n4_bit_load_with_counter_register_3_cout), .Outputs(Outputs[16:13]));
  and and_3 (and_3_out, and_4_out, n4_bit_load_with_counter_register_4_cout);
  _4_bit_load_with_counter_register u_4_bit_load_with_counter_register_4 (
    .count(and_4_out), .load(load), .Input(Input[12:9]), .clock(clock), .clear(clear),
    .Cout(n4_bit_load_with_counter_register_4_cout), .Outputs(Outputs[12:9]));
  and and_4 (and_4_out, and_5_out, n4_bit_load_with_counter_register_5_cout);
  and and_5 (and_5_out, and_6_out, n4_bit_load_with_counter_register_6_cout);
  _4_bit_load_with_counter_register u_4_bit_load_with_counter_register_5 (
    .count(and_5_out), .load(load), .Input(Input[8:5]), .clock(clock), .clear(clear),
    .Cout(n4_bit_load_with_counter_register_5_cout), .Outputs(Outputs[8:5]));
  and and_6 (and_6_out, count, n1_bit_load_with_counter_register_1_cout);
  _4_bit_load_with_counter_register u_4_bit_load_with_counter_register_6 (
    .count(and_6_out), .load(load), .Input(Input[4:1]), .clock(clock), .clear(clear),
    .Cout(n4_bit_load_with_counter_register_6_cout), .Outputs(Outputs[4:1]));
  _1_bit_load_with_counter_register u_1_bit_load_with_counter_register_1 (
    .count(count), .load(load), .Input(Input[0]), .clock(clock), .clear(clear),
    .Cout(n1_bit_load_with_counter_register_1_cout), .Outputs(Outputs[0]));
endmodule

// CU
module Control_Unit (
  input  Reset,
  input  clock,
  input  [24:0] Memory_Out,
  output [5:0] Address_Bus,
  output [24:0] Memory_Input_Value,
  output Clock_2,
  output Memory_Store,
  output [24:0] Acc_Out
);

  wire ACC_to_MBR, ADD, AND, and_8_out, and_35_out, and_36_out, BSB_inc_PC, BSB_load_PC, BSB_store_MEM, BUN,
       DIV_Store_to_ACC, execution_cycle, F, Halt, Hold_Counter, inc_pc, ISZ_inc_MBR, ISZ_inc_PC, JN_load_PC,
       JZ_load_PC, Load_ACC, load_IR, load_MAR, load_MBR, MBR_to_ACC, MBR_to_MAR, MBR_to_MEM, MEM_to_MBR_var,
       MUL_Apply_Clock, MUL_Reset, MUL_Store_to_ACC, NEG, not_1_out, not_2_out, not_3_out, or_2_out,
       or_3_out, or_4_out, or_5_out, or_6_out, or_7_out, or_8_out, or_9_out, or_10_out, or_11_out, or_12_out,
       or_14_out, or_15_out, or_16_out, or_17_out, or_18_out, or_19_out, POP_MBR_to_ACC, POP_MEM_to_MBR,
       POP_SR_to_MAR, priority_encoder_1_out, PUSH_AC_to_MBR, PUSH_MBR_to_MEM, PUSH_SR_to_MAR, q0, q1, q2,
       q3, q4, q5, q6, q7, q8, q9, q10, q11, q12, q13, q14, q15, REM_Store_to_ACC, Return_Fetch_Cycle, S_qn,
       sign_flag_1_out_2, t0, t1, t2, t3, zero_flag_1_out_2, zero_flag_2_out_2;
  wire [1:0] n2_bit_counter_1_out_4, priority_encoder_2_p2;
  wire [3:0] n4_bit_load_register_1_output, Stack_Address;
  wire [5:0] Address_from_Code, n2x1_mux_6_bit_1_out_4, n2x1_mux_6_bit_2_out_4, PC_Out;
  wire [24:0] ACC_In, ALU_MBR_Out, ALU_Out, DIV_Out, MUL_Out, n2x1_mux_25_bit_1_out_4,
       n2x1_mux_25_bit_3_out_4, n2x1_mux_25_bit_4_out_4, n2x1_mux_25_bit_7_out_4, REM_Out;
  wire [24:6] bit_extender_1_out, MBR_Out;

  and and_1 (AND, t2, q0, F);
  D_Flip_Flop S (.clk(Clock_2), .D(Halt), .Qn(S_qn), .reset(Reset));  // open: Q, preset, en
  _2_bit_Counter u_2_bit_counter_1 (
    .Clock(Clock_2), .Reset(Reset), .out_4(n2_bit_counter_1_out_4), .hold(Hold_Counter));
  and and_2 (load_MAR, ~F, t0);  // AND_Gate
  and and_3 (JZ_load_PC, t3, zero_flag_1_out_2, q7);
  and and_4 (MBR_to_MAR, t0, not_1_out, F);
  and and_5 (BSB_store_MEM, t1, q4, F);
  and and_6 (PUSH_SR_to_MAR, t0, q8, F);
  and and_7 (POP_SR_to_MAR, t1, q9, F);
  and and_8 (and_8_out, t1, q12, F);
  or or_1 (MUL_Reset, and_8_out, Reset);
  and and_9 (DIV_Store_to_ACC, t2, q13, F);
  and and_10 (Clock_2, clock, S_qn);
  Decoder #(.select(2)) decoder_1 (
    .out0(t0), .out1(t1), .out2(t2), .out3(t3), .sel(n2_bit_counter_1_out_4));  // open: en
  Priority_Encoder #(.select(1), .disabled(0)) priority_encoder_1 (
    .in0(Return_Fetch_Cycle), .in1(execution_cycle), .out(priority_encoder_1_out));  // open: gs, en_out, en_in
  _4_bit_load_register u_4_bit_load_register_1 (
    .load(load_IR), .Input(MBR_Out[23:20]), .clock(Clock_2), .clear(Reset),
    .Output(n4_bit_load_register_1_output));
  Zero_Flag zero_flag_1 (.in_1(Acc_Out), .out_2(zero_flag_1_out_2));
  not not_1 (not_1_out, or_2_out);
  or or_2 (or_2_out, q8, q9);
  D_Flip_Flop #(.trigger("falling")) u_F (
    .clk(Clock_2), .D(priority_encoder_1_out), .Q(F), .reset(Reset));  // open: Qn, preset, en
  Decoder #(.select(4)) decoder_2 (
    .out0(q0), .out1(q1), .out2(q2), .out3(q3), .out4(q4), .out5(q5), .out6(q6), .out7(q7), .out8(q8),
    .out9(q9), .out10(q10), .out11(q11), .out12(q12), .out13(q13), .out14(q14), .out15(q15),
    .sel(n4_bit_load_register_1_output));  // open: en
  or or_3 (or_3_out, AND, ~AND);  // OR_Gate
  // Priority_Encoder #(.select(2)) priority_encoder_2: pin names not known; wires that end beside it: or_3_out, priority_encoder_2_p2, ADD, NEG
  _2x1_Mux_25_bit u_2x1_mux_25_bit_1 (
    .input1({MBR_Out, Address_from_Code}), .input2({25{1'b0}}), .out_4(n2x1_mux_25_bit_1_out_4),
    .selection_bit(NEG));
  and and_11 (inc_pc, ~F, t1);  // AND_Gate
  and and_12 (ADD, t2, q1, F);
  and and_13 (BSB_load_PC, t2, q4, F);
  and and_14 (REM_Store_to_ACC, t2, q14, F);
  // Probe on PC_Out
  ALU alu_1 (
    .A(n2x1_mux_25_bit_1_out_4), .B(Acc_Out), .Control_or_and_add_sub(priority_encoder_2_p2), .Result(ALU_Out));  // open: flags_NZOC
  and and_15 (JN_load_PC, t3, sign_flag_1_out_2, q15);
  and and_16 (Return_Fetch_Cycle, t3, F);
  and and_17 (PUSH_AC_to_MBR, t1, q8, F);
  and and_18 (POP_MEM_to_MBR, t2, q9, F);
  and and_19 (MUL_Store_to_ACC, t3, q12, F);
  and and_20 (load_MBR, ~F, t1);  // AND_Gate
  Sign_Flag sign_flag_1 (.in_1(Acc_Out), .out_2(sign_flag_1_out_2));
  and and_21 (Load_ACC, t2, or_4_out, F);
  // Probe on Address_Bus
  // Probe on {2'b11, Stack_Address}
  and and_22 (Halt, t0, q10, F);
  or or_4 (or_4_out, q0, q1);
  and and_23 (BSB_inc_PC, t3, q4, F);
  // Probe on {MBR_Out, Address_from_Code}
  and and_24 (load_IR, ~F, t2);  // AND_Gate
  and and_25 (MUL_Apply_Clock, q12, Clock_2, F);
  Divider #(.width(25)) divider_1 (
    .a(Acc_Out), .b({MBR_Out, Address_from_Code}), .out(DIV_Out), .rem(REM_Out));  // open: upper
  // Probe on Acc_Out
  and and_26 (PUSH_MBR_to_MEM, t2, q8, F);
  and and_27 (POP_MBR_to_ACC, t3, q9, F);
  // Probe on Acc_Out
  or or_5 (or_5_out, inc_pc, ISZ_inc_PC, BSB_inc_PC);
  PC pc_1 (
    .count(or_5_out), .load(or_6_out), .clock(Clock_2), .clear(Reset), .Input(Address_from_Code),
    .Outputs(PC_Out));
  or or_6 (or_6_out, BSB_load_PC, BUN, JZ_load_PC, JN_load_PC);
  or or_7 (or_7_out, MBR_to_ACC, POP_MBR_to_ACC);
  or or_8 (or_8_out, DIV_Store_to_ACC, REM_Store_to_ACC);
  and and_28 (MEM_to_MBR_var, t1, or_10_out, F);
  and and_29 (ACC_to_MBR, t2, q2, F);
  and and_30 (ISZ_inc_MBR, t2, q6, F);
  _2x1_Mux_25_bit u_2x1_mux_25_bit_2 (
    .input1(ALU_Out), .input2({MBR_Out, Address_from_Code}), .out_4(ALU_MBR_Out), .selection_bit(or_7_out));
  or or_9 (or_9_out, or_7_out, NEG, Load_ACC, MUL_Store_to_ACC, or_8_out);
  and and_31 (BUN, t3, q3);
  or or_10 (or_10_out, q0, q13, q1, q6, q5, q2, or_11_out);
  Accumulator accumulator_1 (.clock(Clock_2), .load(or_9_out), .clear(Reset), .\input (ACC_In), .\output (Acc_Out));
  or or_11 (or_11_out, q12, q14);
  _2x1_Mux_25_bit u_2x1_mux_25_bit_3 (
    .input1(ALU_MBR_Out), .input2(MUL_Out), .out_4(n2x1_mux_25_bit_3_out_4), .selection_bit(MUL_Store_to_ACC));
  not not_2 (not_2_out, BSB_store_MEM);
  assign {bit_extender_1_out[24:22], bit_extender_1_out[19:6]} = {{16{1'b0}}, not_2_out};  // Bit_Extender bit_extender_1
  and and_32 (NEG, t3, q11);
  and and_33 (MBR_to_MEM, t3, q2, F);
  and and_34 (ISZ_inc_PC, t3, q6, zero_flag_2_out_2, F);
  and and_35 (and_35_out, t3, q8, F, Clock_2);
  or or_12 (or_12_out, and_35_out, and_36_out);
  and and_36 (and_36_out, Clock_2, t0, q9, F);
  _25_bit_multiplier u_25_bit_multiplier_1 (
    .M_input({MBR_Out, Address_from_Code}), .Q_input(Acc_Out), .Reset(MUL_Reset), .clock(MUL_Apply_Clock),
    .Running(Hold_Counter), .out_7(MUL_Out));  // open: out_6
  _2x1_Mux_25_bit u_2x1_mux_25_bit_4 (
    .input1(n2x1_mux_25_bit_3_out_4), .input2(DIV_Out), .out_4(n2x1_mux_25_bit_4_out_4),
    .selection_bit(DIV_Store_to_ACC));
  _2x1_Mux_25_bit u_2x1_mux_25_bit_5 (
    .input1({MBR_Out, Address_from_Code}),
    .input2({bit_extender_1_out[24:22], {2{BSB_store_MEM}}, bit_extender_1_out[19:6], PC_Out}),
    .out_4(Memory_Input_Value), .selection_bit(BSB_store_MEM));
  _4_bit_Stack_Register u_4_bit_stack_register_1 (
    .clock(or_12_out), .Increment(and_36_out), .clear(Reset), .out_4(Stack_Address));
  _2x1_Mux_25_bit u_2x1_mux_25_bit_6 (
    .input1(n2x1_mux_25_bit_4_out_4), .input2(REM_Out), .out_4(ACC_In), .selection_bit(REM_Store_to_ACC));
  or or_13 (Memory_Store, MBR_to_MEM, BSB_store_MEM, PUSH_MBR_to_MEM);
  Zero_Flag zero_flag_2 (.in_1({MBR_Out, Address_from_Code}), .out_2(zero_flag_2_out_2));
  _2x1_Mux_6_bit u_2x1_mux_6_bit_1 (
    .input1(PC_Out), .input2(Address_from_Code), .out_4(n2x1_mux_6_bit_1_out_4), .selection_bit(MBR_to_MAR));
  or or_14 (or_14_out, PUSH_SR_to_MAR, POP_SR_to_MAR);
  or or_15 (or_15_out, PUSH_AC_to_MBR, ACC_to_MBR);
  or or_16 (or_16_out, MEM_to_MBR_var, POP_MEM_to_MBR);
  and and_37 (execution_cycle, ~F, not_3_out, t3);  // AND_Gate
  and and_38 (MBR_to_ACC, t2, q5, F);
  _2x1_Mux_6_bit u_2x1_mux_6_bit_2 (
    .input1(n2x1_mux_6_bit_1_out_4), .input2({2'b11, Stack_Address}), .out_4(n2x1_mux_6_bit_2_out_4),
    .selection_bit(or_14_out));
  MAR mar_1 (
    .clock(Clock_2), .load(or_17_out), .clear(Reset), .\input (n2x1_mux_6_bit_2_out_4), .\output (Address_Bus));
  or or_17 (or_17_out, or_14_out, MBR_to_MAR, load_MAR);
  _2x1_Mux_25_bit u_2x1_mux_25_bit_7 (
    .input1(Memory_Out), .input2(Acc_Out), .out_4(n2x1_mux_25_bit_7_out_4), .selection_bit(or_15_out));
  or or_18 (or_18_out, or_15_out, load_MBR, or_16_out);
  MBR mbr_1 (
    .count(ISZ_inc_MBR), .load(or_18_out), .clock(Clock_2), .clear(Reset), .Input(n2x1_mux_25_bit_7_out_4),
    .Outputs({MBR_Out, Address_from_Code}));
  not not_3 (not_3_out, or_19_out);
  or or_19 (or_19_out, q3, q7, q11, q15);

  // Other names for the same wires on the sheet: clear = Reset; clock_t = Clock_2; MAR_Out[5:0] = Address_Bus;
  //   MBR_Out[5:0] = Address_from_Code; OP_Code[3:0] = MBR_Out[23:20]; MEM_Out[24:0] = Memory_Out

  // Notes on the sheet:
  //   JUMP
  //   For BSB:
  //   For PUSH/POP
  //   Multiplication
  //   Division and Reminder
  //   Fetch Cycle
  //   Execution Cycle
  //   AND
  //   ADD
  //   STORE
  //   BUN
  //   JN
  //   BSB
  //   LOAD
  //   ISZ
  //   JZ
  //   PUSH
  //   POP
  //   HALT
  //   NEG
  //   MUL
  //   Program Counter
  //   Accumulator
  //   For ISZ:
  //   MAR
  //   Buffer Register
endmodule

module _2_bit_Counter (
  input  hold,
  input  Clock,
  input  Reset,
  output [1:0] out_4
);

  wire and_1_out, d_ff_1_qn, d_ff_2_qn, not_1_out;

  not not_1 (not_1_out, hold);
  and and_1 (and_1_out, not_1_out, Clock);
  D_Flip_Flop #(.trigger("falling")) d_ff_1 (
    .clk(and_1_out), .D(d_ff_1_qn), .Q(out_4[0]), .Qn(d_ff_1_qn), .reset(Reset));  // open: preset, en
  D_Flip_Flop #(.trigger("falling")) d_ff_2 (
    .clk(out_4[0]), .D(d_ff_2_qn), .Q(out_4[1]), .Qn(d_ff_2_qn), .reset(Reset));  // open: preset, en
endmodule

module _2x1_Mux_25_bit (
  input  [24:0] input1,
  input  [24:0] input2,
  input  selection_bit,
  output [24:0] out_4
);

  wire [24:0] and_1_out, and_2_out;

  assign and_1_out = input1 & ~{25{selection_bit}};  // AND_Gate and_1, 25 bits wide
  assign and_2_out = {25{selection_bit}} & input2;  // AND_Gate and_2, 25 bits wide
  assign out_4 = and_1_out | and_2_out;  // OR_Gate or_1, 25 bits wide
endmodule

module _2x1_Mux_6_bit (
  input  [5:0] input1,
  input  [5:0] input2,
  input  selection_bit,
  output [5:0] out_4
);

  wire [5:0] and_1_out, and_2_out;

  assign and_1_out = input1 & ~{6{selection_bit}};  // AND_Gate and_1, 6 bits wide
  assign and_2_out = {6{selection_bit}} & input2;  // AND_Gate and_2, 6 bits wide
  assign out_4 = and_1_out | and_2_out;  // OR_Gate or_1, 6 bits wide
endmodule

module _4_bit_Stack_Register (
  input  clock,
  input  Increment,
  input  clear,
  output [3:0] out_4
);

  wire and_1_out, and_2_out, and_3_out, and_4_out, and_5_out, and_6_out, or_1_out, or_2_out, or_3_out,
       t_ff_1_q, t_ff_2_q, t_ff_3_q;

  and and_1 (and_1_out, ~Increment, t_ff_1_q);  // AND_Gate
  T_Flip_Flop #(.trigger("falling")) t_ff_1 (
    .clk(clock), .T(1'b1), .Q(t_ff_1_q), .Qn(out_4[0]), .reset(clear));  // open: preset, en
  and and_2 (and_2_out, out_4[0], Increment);
  T_Flip_Flop #(.trigger("falling")) t_ff_2 (
    .clk(clock), .T(or_1_out), .Q(t_ff_2_q), .Qn(out_4[1]), .reset(clear));  // open: preset, en
  or or_1 (or_1_out, and_1_out, and_2_out);
  and and_3 (and_3_out, and_1_out, t_ff_2_q);
  and and_4 (and_4_out, out_4[1], and_2_out);
  T_Flip_Flop #(.trigger("falling")) t_ff_3 (
    .clk(clock), .T(or_2_out), .Q(t_ff_3_q), .Qn(out_4[2]), .reset(clear));  // open: preset, en
  or or_2 (or_2_out, and_3_out, and_4_out);
  and and_5 (and_5_out, and_3_out, t_ff_3_q);
  or or_3 (or_3_out, and_5_out, and_6_out);
  and and_6 (and_6_out, out_4[2], and_4_out);
  T_Flip_Flop #(.trigger("falling")) t_ff_4 (
    .clk(clock), .T(or_3_out), .Qn(out_4[3]), .reset(clear));  // open: Q, preset, en
  // Probe on out_4
endmodule
